// Logisim project cpu.circ as structural Verilog: 2 circuits, main circuit main
module main (
  input  [15:0] INSTRUCTION,
  input  CLOCK,
  output [15:0] FETCH_ADDRESS,
  output Overflow,
  output [15:0] s0_Value,
  output [15:0] s1_Value,
  output [15:0] s2_Value,
  output [15:0] ra_Value,
  output [15:0] sp_Value,
  output [15:0] HI_Value,
  output [15:0] LO_Value
);

  wire MEM_p1, MEM_p3, MEM_p6, MEM_p9, MEM_p12;

  Register #(.width(16)) PC ();  // open: D, en, Q, clk, clr
  Register #(.width(16)) LO ();  // open: D, en, Q, clk, clr
  Register #(.width(16)) HI ();  // open: D, en, Q, clk, clr
  // regfile_main main_1: pin names not known
  // alu_main main_2: pin names not known
  // mem_main MEM: pin names not known; wires that end beside it: MEM_p1, s0_Value, MEM_p3, MEM_p3, s1_Value, MEM_p6, MEM_p6, s2_Value, MEM_p9, MEM_p9, ra_Value, MEM_p12, MEM_p12, sp_Value

  // Other names for the same wires on the sheet: clk = CLOCK; fetch_addr[15:0] = FETCH_ADDRESS

  // Notes on the sheet:
  //   Output
  //   These are outputs/inputs from run.circ
  //   Inputs
  //   These are DEBUG/TEST outputs from your circuit.
endmodule

module control_signal (
  input  [15:0] Input
);
endmodule
